# Fritzing sketch 1_shift_register_4_outputs_4_inputs (saved by Fritzing 0.9.6b)
breadboards: 2

parts:
  Part2 = Arduino Uno (Rev3) - ICSP
  U3 = 74HC595 [package="DIP16 [THT]"]
  R13 = Resistor [tolerance=±5% resistance=330 package="2512 [SMD]"]
  R14 = Resistor [tolerance=±5% resistance=330 package="2512 [SMD]"]
  R16 = Resistor [tolerance=±5% resistance=330 package="2512 [SMD]"]
  R17 = Resistor [tolerance=±5% resistance=330 package="2512 [SMD]"]
  LED9 = smd LED [color="Red (633nm)" package="1206 [SMD]"]
  LED12 = smd LED [color="Red (633nm)" package="1206 [SMD]"]
  LED15 = smd LED [color="Red (633nm)" package="1206 [SMD]"]
  D24 = Rectifier Diode [part_number=1N4001 package="300 mil [THT]"]
  Diode1 = Rectifier Diode [part_number=1N4001 package="300 mil [THT]"]
  D26 = Rectifier Diode [part_number=1N4001 package="300 mil [THT]"]
  D28 = Rectifier Diode [part_number=1N4001 package="300 mil [THT]"]
  LED16 = smd LED [color="Red (633nm)" package="1206 [SMD]"]
  S17 = Momentary Switch [package=ksa_sealed_tac_switch]
  S19 = Momentary Switch [package=ksa_sealed_tac_switch]
  S20 = Momentary Switch [package=ksa_sealed_tac_switch]
  S23 = Momentary Switch [package=ksa_sealed_tac_switch]
  R21 = Resistor [tolerance=±5% resistance=10k package="2512 [SMD]"]
  C6 = Tantalum Capacitor [capacitance="1 μF" voltage=35V package="B 3528 [SMD, tantalum]"]
  C8 = Electrolytic Capacitor [capacitance=10μF voltage=35V package="0605 [SMD, electrolytic]"]

nets:
  N1: Part2.ICSP_MISO, Part2.D12/MISO, U3.DS
  N2: Part2.D8, U3.ST_CP
  N3: Part2.D2, S17.1, S19.1, S20.1, S23.1, R21.Pin_0
  N4: Part2.D7, U3.SH_CP
  5V: Part2.5V, U3.MR, U3.VCC, C6.+, C8.+
  N5: Part2.GND, U3.OE, R13.Pin_0, R14.Pin_0, R16.Pin_0, R17.Pin_0, R21.Pin_1, C6.-, C8.-
  N6: U3.Q1, LED12.cathode
  N7: U3.Q2, LED9.cathode
  N8: U3.Q3, LED15.cathode
  N9: U3.Q4, D24.anode
  N10: U3.Q5, D26.anode
  N11: U3.Q6, D28.anode
  N12: U3.Q7, Diode1.anode
  N13: U3.Q0, LED16.cathode
  N14: R13.Pin_1, LED12.anode
  N15: R14.Pin_1, LED15.anode
  N16: R16.Pin_1, LED9.anode
  N17: R17.Pin_1, LED16.anode
  N18: D24.cathode, S19.4
  N19: Diode1.cathode, S17.4
  N20: D26.cathode, S20.4
  N21: D28.cathode, S23.4
