# Fritzing sketch 2_shift_registers_8_outputs_8_inputs (saved by Fritzing 0.9.6b)
breadboards: 2

parts:
  Part1 = Arduino Uno (Rev3) - ICSP
  U1 = 74HC595 [package="DIP16 [THT]"]
  U2 = 74HC595 [package="DIP16 [THT]"]
  R1 = Resistor [tolerance=±5% resistance=330 package="2512 [SMD]"]
  R2 = Resistor [tolerance=±5% resistance=330 package="2512 [SMD]"]
  R3 = Resistor [tolerance=±5% resistance=330 package="2512 [SMD]"]
  R4 = Resistor [tolerance=±5% resistance=330 package="2512 [SMD]"]
  R5 = Resistor [tolerance=±5% resistance=330 package="2512 [SMD]"]
  R6 = Resistor [tolerance=±5% resistance=330 package="2512 [SMD]"]
  R10 = Resistor [tolerance=±5% resistance=330 package="2512 [SMD]"]
  R11 = Resistor [tolerance=±5% resistance=330 package="2512 [SMD]"]
  LED1 = smd LED [color="Red (633nm)" package="1206 [SMD]"]
  LED2 = smd LED [color="Red (633nm)" package="1206 [SMD]"]
  LED3 = smd LED [color="Red (633nm)" package="1206 [SMD]"]
  LED4 = smd LED [color="Red (633nm)" package="1206 [SMD]"]
  LED5 = smd LED [color="Red (633nm)" package="1206 [SMD]"]
  LED6 = smd LED [color="Red (633nm)" package="1206 [SMD]"]
  LED7 = smd LED [color="Red (633nm)" package="1206 [SMD]"]
  LED8 = smd LED [color="Red (633nm)" package="1206 [SMD]"]
  D15 = Rectifier Diode [part_number=1N4001 package="300 mil [THT]"]
  D16 = Rectifier Diode [part_number=1N4001 package="300 mil [THT]"]
  D17 = Rectifier Diode [part_number=1N4001 package="300 mil [THT]"]
  D18 = Rectifier Diode [part_number=1N4001 package="300 mil [THT]"]
  D19 = Rectifier Diode [part_number=1N4001 package="300 mil [THT]"]
  D20 = Rectifier Diode [part_number=1N4001 package="300 mil [THT]"]
  D22 = Rectifier Diode [part_number=1N4001 package="300 mil [THT]"]
  Diode = Rectifier Diode [part_number=1N4001 package="300 mil [THT]"]
  S8 = Momentary Switch [package=ksa_sealed_tac_switch]
  S9 = Momentary Switch [package=ksa_sealed_tac_switch]
  S10 = Momentary Switch [package=ksa_sealed_tac_switch]
  S11 = Momentary Switch [package=ksa_sealed_tac_switch]
  S12 = Momentary Switch [package=ksa_sealed_tac_switch]
  S13 = Momentary Switch [package=ksa_sealed_tac_switch]
  S14 = Momentary Switch [package=ksa_sealed_tac_switch]
  S15 = Momentary Switch [package=ksa_sealed_tac_switch]
  R12 = Resistor [tolerance=±5% resistance=10k package="2512 [SMD]"]
  C2 = Tantalum Capacitor [capacitance="1 μF" voltage=35V package="B 3528 [SMD, tantalum]"]
  C3 = Tantalum Capacitor [capacitance="1 μF" voltage=35V package="B 3528 [SMD, tantalum]"]
  C5 = Electrolytic Capacitor [capacitance=10μF voltage=35V package="0605 [SMD, electrolytic]"]

nets:
  N1: Part1.ICSP_MISO, Part1.D12/MISO, U1.DS
  N2: Part1.D8, U1.ST_CP, U2.ST_CP
  N3: Part1.D2, S8.1, S9.1, S10.1, S11.1, S12.1, S13.1, S14.1, S15.1, R12.Pin_0
  N4: Part1.D7, U1.SH_CP, U2.SH_CP
  VCC: Part1.5V, U1.MR, U1.VCC, U2.MR, U2.VCC, C2.+, C3.+, C5.+
  N5: Part1.GND, U1.OE, U2.OE, R1.Pin_0, R2.Pin_0, R3.Pin_0, R4.Pin_0, R5.Pin_0, R6.Pin_0, R10.Pin_0, R11.Pin_0, R12.Pin_1, C2.-, C3.-, C5.-
  N6: U1.Q1, LED2.cathode
  N7: U1.Q2, LED3.cathode
  N8: U1.Q3, LED4.cathode
  N9: U1.Q4, LED8.cathode
  N10: U1.Q5, LED6.cathode
  N11: U1.Q6, LED5.cathode
  N12: U1.Q7, LED7.cathode
  N13: U1.Q7', U2.DS
  N14: U1.Q0, LED1.cathode
  N15: U2.Q1, D16.anode
  N16: U2.Q2, D18.anode
  N17: U2.Q3, D17.anode
  N18: U2.Q4, D19.anode
  N19: U2.Q5, D20.anode
  N20: U2.Q6, D22.anode
  N21: U2.Q7, Diode.anode
  N22: U2.Q0, D15.anode
  N23: R1.Pin_1, LED3.anode
  N24: R2.Pin_1, LED2.anode
  N25: R3.Pin_1, LED1.anode
  N26: R4.Pin_1, LED8.anode
  N27: R5.Pin_1, LED4.anode
  N28: R6.Pin_1, LED6.anode
  N29: R10.Pin_1, LED7.anode
  N30: R11.Pin_1, LED5.anode
  N31: D15.cathode, S8.4
  N32: D16.cathode, S9.4
  N33: D17.cathode, S10.4
  N34: D18.cathode, S11.4
  N35: D19.cathode, S12.4
  N36: D20.cathode, S13.4
  N37: D22.cathode, S15.4
  N38: Diode.cathode, S14.4
