# Fritzing sketch 3_shift_registers_11_outputs_12_inputs (saved by Fritzing 0.9.6b)
breadboards: 2

parts:
  Part1 = Arduino Uno (Rev3) - ICSP
  U1 = 74HC595 [package="DIP16 [THT]"]
  U2 = 74HC595 [package="DIP16 [THT]"]
  R1 = Resistor [tolerance=±5% resistance=330 package="2512 [SMD]"]
  R2 = Resistor [tolerance=±5% resistance=330 package="2512 [SMD]"]
  R3 = Resistor [tolerance=±5% resistance=330 package="2512 [SMD]"]
  R4 = Resistor [tolerance=±5% resistance=330 package="2512 [SMD]"]
  R5 = Resistor [tolerance=±5% resistance=330 package="2512 [SMD]"]
  R6 = Resistor [tolerance=±5% resistance=330 package="2512 [SMD]"]
  R7 = Resistor [tolerance=±5% resistance=330 package="2512 [SMD]"]
  R8 = Resistor [tolerance=±5% resistance=330 package="2512 [SMD]"]
  R9 = Resistor [tolerance=±5% resistance=330 package="2512 [SMD]"]
  R10 = Resistor [tolerance=±5% resistance=330 package="2512 [SMD]"]
  R11 = Resistor [tolerance=±5% resistance=330 package="2512 [SMD]"]
  LED1 = smd LED [color="Red (633nm)" package="1206 [SMD]"]
  LED2 = smd LED [color="Red (633nm)" package="1206 [SMD]"]
  LED3 = smd LED [color="Red (633nm)" package="1206 [SMD]"]
  LED4 = smd LED [color="Red (633nm)" package="1206 [SMD]"]
  LED5 = smd LED [color="Red (633nm)" package="1206 [SMD]"]
  LED6 = smd LED [color="Red (633nm)" package="1206 [SMD]"]
  LED7 = smd LED [color="Red (633nm)" package="1206 [SMD]"]
  LED8 = smd LED [color="Red (633nm)" package="1206 [SMD]"]
  LED9 = smd LED [color="Red (633nm)" package="1206 [SMD]"]
  LED10 = smd LED [color="Red (633nm)" package="1206 [SMD]"]
  LED12 = smd LED [color="Red (633nm)" package="1206 [SMD]"]
  U3 = 74HC595 [package="DIP16 [THT]"]
  D15 = Rectifier Diode [part_number=1N4001 package="300 mil [THT]"]
  D16 = Rectifier Diode [part_number=1N4001 package="300 mil [THT]"]
  D17 = Rectifier Diode [part_number=1N4001 package="300 mil [THT]"]
  D18 = Rectifier Diode [part_number=1N4001 package="300 mil [THT]"]
  D19 = Rectifier Diode [part_number=1N4001 package="300 mil [THT]"]
  D20 = Rectifier Diode [part_number=1N4001 package="300 mil [THT]"]
  D21 = Rectifier Diode [part_number=1N4001 package="300 mil [THT]"]
  D22 = Rectifier Diode [part_number=1N4001 package="300 mil [THT]"]
  D23 = Rectifier Diode [part_number=1N4001 package="300 mil [THT]"]
  D24 = Rectifier Diode [part_number=1N4001 package="300 mil [THT]"]
  D25 = Rectifier Diode [part_number=1N4001 package="300 mil [THT]"]
  Diode = Rectifier Diode [part_number=1N4001 package="300 mil [THT]"]
  S8 = Momentary Switch [package=ksa_sealed_tac_switch]
  S9 = Momentary Switch [package=ksa_sealed_tac_switch]
  S10 = Momentary Switch [package=ksa_sealed_tac_switch]
  S11 = Momentary Switch [package=ksa_sealed_tac_switch]
  S12 = Momentary Switch [package=ksa_sealed_tac_switch]
  S13 = Momentary Switch [package=ksa_sealed_tac_switch]
  S14 = Momentary Switch [package=ksa_sealed_tac_switch]
  S15 = Momentary Switch [package=ksa_sealed_tac_switch]
  S16 = Momentary Switch [package=ksa_sealed_tac_switch]
  S17 = Momentary Switch [package=ksa_sealed_tac_switch]
  S18 = Momentary Switch [package=ksa_sealed_tac_switch]
  S19 = Momentary Switch [package=ksa_sealed_tac_switch]
  R12 = Resistor [tolerance=±5% resistance=10k package="2512 [SMD]"]
  C2 = Tantalum Capacitor [capacitance="1 μF" voltage=35V package="B 3528 [SMD, tantalum]"]
  C3 = Tantalum Capacitor [capacitance="1 μF" voltage=35V package="B 3528 [SMD, tantalum]"]
  C4 = Tantalum Capacitor [capacitance="1 μF" voltage=35V package="B 3528 [SMD, tantalum]"]
  C5 = Electrolytic Capacitor [capacitance=10μF voltage=35V package="0605 [SMD, electrolytic]"]

nets:
  N1: Part1.ICSP_MISO, Part1.D12/MISO, U1.DS
  N2: Part1.D8, U1.ST_CP, U2.ST_CP, U3.ST_CP
  N3: Part1.D2, S8.1, S9.1, S10.1, S11.1, S12.1, S13.1, S14.1, S15.1, S16.1, S17.1, S18.1, S19.1, R12.Pin_0
  N4: Part1.D7, U1.SH_CP, U2.SH_CP, U3.SH_CP
  VCC: Part1.5V, U1.MR, U1.VCC, U2.MR, U2.VCC, U3.MR, U3.VCC, C2.+, C3.+, C4.+, C5.+
  GND: Part1.GND, U1.OE, U2.OE, R1.Pin_0, R2.Pin_0, R3.Pin_0, R4.Pin_0, R5.Pin_0, R6.Pin_0, R7.Pin_0, R8.Pin_0, R9.Pin_0, R10.Pin_0, R11.Pin_0, U3.Q7, U3.GND, U3.OE, R12.Pin_1, C2.-, C3.-, C4.-, C5.-
  N5: U1.Q1, LED2.cathode
  N6: U1.Q2, LED3.cathode
  N7: U1.Q3, LED4.cathode
  N8: U1.Q4, LED8.cathode
  N9: U1.Q5, LED6.cathode
  N10: U1.Q6, LED5.cathode
  N11: U1.Q7, LED7.cathode
  N12: U1.Q7', U2.DS
  N13: U1.Q0, LED1.cathode
  N14: U2.Q1, LED10.cathode
  N15: U2.Q2, LED9.cathode
  N16: U2.Q3, U2.Q4, D18.anode
  N17: U2.Q5, D16.anode
  N18: U2.Q6, D17.anode
  N19: U2.Q7, D20.anode
  N20: U2.Q7', U3.DS
  N21: U2.Q0, LED12.cathode
  N22: R1.Pin_1, LED3.anode
  N23: R2.Pin_1, LED2.anode
  N24: R3.Pin_1, LED1.anode
  N25: R4.Pin_1, LED8.anode
  N26: R5.Pin_1, LED4.anode
  N27: R6.Pin_1, LED6.anode
  N28: R7.Pin_1, LED9.anode
  N29: R8.Pin_1, LED10.anode
  N30: R9.Pin_1, LED12.anode
  N31: R10.Pin_1, LED7.anode
  N32: R11.Pin_1, LED5.anode
  N33: U3.Q1, D22.anode
  N34: U3.Q2, D24.anode
  N35: U3.Q3, D23.anode
  N36: U3.Q4, D21.anode
  N37: U3.Q5, D25.anode
  N38: U3.Q6, Diode.anode
  N39: U3.Q0, D19.anode
  N40: D15.cathode, S8.4
  N41: D16.cathode, S9.4
  N42: D17.cathode, S10.4
  N43: D18.cathode, S11.4
  N44: D19.cathode, S12.4
  N45: D20.cathode, S13.4
  N46: D21.cathode, S19.4
  N47: D22.cathode, S15.4
  N48: D23.cathode, S16.4
  N49: D24.cathode, S14.4
  N50: D25.cathode, S17.4
  N51: Diode.cathode, S18.4
